// Logisim project Assignment3 (2).circ as structural Verilog: 3 circuits, main circuit ALU
module ALU (
  input  [2:0] op,
  input  [15:0] a,
  input  [15:0] b,
  output [15:0] out,
  output zero
);

  wire [15:0] adder_1_out, adder_2_out, adder_3_out, adder_4_out, adder_5_out, and_1_out, and_2_out,
       multiplexer_1_out, not_1_out, not_2_out, not_3_out, not_4_out, or_1_out, or_2_out;

  assign not_1_out = ~b;  // NOT_Gate not_1, 16 bits wide
  Adder #(.width(16)) adder_1 (.a(not_1_out), .b(16'h1), .out(adder_1_out));  // open: cin, cout
  assign not_2_out = ~b;  // NOT_Gate not_2, 16 bits wide
  Adder #(.width(16)) adder_2 (.a(not_2_out), .b(16'h1), .out(adder_2_out));  // open: cin, cout
  Adder #(.width(16)) adder_3 (.a(a), .b(adder_1_out), .out(adder_3_out));  // open: cin, cout
  assign and_1_out = a & b;  // AND_Gate and_1, 16 bits wide
  assign or_1_out = a | b;  // OR_Gate or_1, 16 bits wide
  Adder #(.width(16)) adder_4 (.a(a), .b(b), .out(adder_4_out));  // open: cin, cout
  assign and_2_out = a & not_3_out;  // AND_Gate and_2, 16 bits wide
  assign not_3_out = ~b;  // NOT_Gate not_3, 16 bits wide
  assign or_2_out = a | not_4_out;  // OR_Gate or_2, 16 bits wide
  assign not_4_out = ~b;  // NOT_Gate not_4, 16 bits wide
  Adder #(.width(16)) adder_5 (.a(a), .b(adder_2_out), .out(adder_5_out));  // open: cin, cout
  Multiplexer #(.enable("false"), .width(16)) multiplexer_1 (
    .in0({16{1'b0}}), .in1(16'h1), .out(multiplexer_1_out), .sel(adder_3_out[15]));
  Multiplexer #(.enable("false"), .select(3), .width(16)) multiplexer_2 (
    .in0(and_1_out), .in1(or_1_out), .in2(adder_4_out), .in4(and_2_out), .in5(or_2_out), .in6(adder_5_out),
    .in7(multiplexer_1_out), .out(out), .sel(op));  // open: in3
  nor nor_1 (zero, out[0], out[1], out[2], out[3], out[4], out[5], out[6], out[7], out[8], out[9], out[10], out[11], out[12], out[13], out[14], out[15]);

  // Notes on the sheet:
  //   This is the brawn of the computer.
  //   The ALU is responsible for performing almost every arithmetic or logical operation
  //   in a modern computer. A premade ALU is provided in the AL
  //   Function:
  //   - If (op == 000), set out = a & b (bitwise AND)
  //   - If (op == 001), set out = a || b (bitwise OR)
  //   - If (op == 010), set out = a + b (addition)
  //   - If (op == 100), set out = a & !b (a and not b)
  //   - If (op == 101), set out = a || !b (a or not b)
  //   - If (op == 110), set out = a - b (subtraction)
  //   - If (op == 111), set out = 0000000000000001 if a < b 
  //   										else 0000000000000000 (set-on-less-than)
  //   - Zero = 1 if (out == 0) else Zero = 0
  //   Hints:
  //   - Tackle the opcodes in the groups described above (first three, next two, and so on)
  //   - For the first three, ignore the MSB of the opcode.
  //   - For the next two, use the MSB to control between negating or not negating B
  //   - At this point, subtraction should be almost implemented.
  //   - Think about two's complement. You have half of two's complement implemented currently.
  //   - You just need to make one connection to fully implement two's complement subtraction
  //   - To determine if A < B, you can use subtraction. 
  //   - If A < B, then A - B should be negative.
  //   - Think about how to determine if a number is negative
  //   - Use that to select between the output for SLT (set on less than)
  //   - Finally, determine how to set the Zero output. You might need to use a splitter for this
endmodule

module Bit (
  input  load,
  input  in,
  output out
);

  wire clock_1_out, multiplexer_1_out;

  Clock clock_1 (.out(clock_1_out));
  Multiplexer #(.enable("false")) multiplexer_1 (.in0(in), .in1(out), .out(multiplexer_1_out), .sel(load));
  D_Flip_Flop d_ff_1 (.D(multiplexer_1_out), .clk(clock_1_out), .Q(out));  // open: Qn, preset, reset

  // Notes on the sheet:
  //   Function:
  //   if load(t-1) then out(t) = in(t-1)
  //   else out(t) = out(t-1)
  //   More simply, when load = 1, 'out' will store the value of 'in' every rising clock edge. When load = 0, 
  //   'out' will not change, even when 'in' changes.
  //   You do not need to use the S, R, or Q-complement ports of the D-FlipFlop
  //   The implementation of this can be found in the lecture slides. 
  //   Take some time to play around with this component (especially the clock) and see how it works.
  //   If you want the clock to automatically tick, go to Simulate>Auto Tick Enabled. You can change
  //   the speed of the clock with Simulate>Auto Tick Frequency
  //   To test this, I recommend turning the Clock to Auto-Tick and verifying that when load is 1, you can
  //   load a value into the flip flop, and when load is 0, the flip flop doesn't change it's value
endmodule

module Register (
  input  load,
  input  [15:0] in,
  output [15:0] out
);

  wire not_1_out;

  not not_1 (not_1_out, load);
  Bit bit_1 (.load(not_1_out), .in(in[0]), .out(out[0]));
  Bit bit_2 (.load(not_1_out), .in(in[1]), .out(out[1]));
  Bit bit_3 (.load(not_1_out), .in(in[2]), .out(out[2]));
  Bit bit_4 (.load(not_1_out), .in(in[3]), .out(out[3]));
  Bit bit_5 (.load(not_1_out), .in(in[4]), .out(out[4]));
  Bit bit_6 (.load(not_1_out), .in(in[5]), .out(out[5]));
  Bit bit_7 (.load(not_1_out), .in(in[6]), .out(out[6]));
  Bit bit_8 (.load(not_1_out), .in(in[7]), .out(out[7]));
  Bit bit_9 (.load(not_1_out), .in(in[8]), .out(out[8]));
  Bit bit_10 (.load(not_1_out), .in(in[9]), .out(out[9]));
  Bit bit_11 (.load(not_1_out), .in(in[10]), .out(out[10]));
  Bit bit_12 (.load(not_1_out), .in(in[11]), .out(out[11]));
  Bit bit_13 (.load(not_1_out), .in(in[12]), .out(out[12]));
  Bit bit_14 (.load(not_1_out), .in(in[13]), .out(out[13]));
  Bit bit_15 (.load(not_1_out), .in(in[14]), .out(out[14]));
  Bit bit_16 (.load(not_1_out), .in(in[15]), .out(out[15]));

  // Notes on the sheet:
  //   Function:
  //   if load(t-1) then out(t) = in(t-1)
  //   else out(t) = out(t-1)
  //   More simply, when load = 1, 'out' will store the value of 'in' every rising clock edge. When load = 0, 
  //   'out' will not change, even when 'in' changes.
  //   The construction of a w-bit Register chip from 1-bit registers is straightforward. All you have
  //   to do is construct an array of w Bit gates and feed the register's load input to every one of them.
  //   To test this, I recommend turning the Clock to Auto-Tick. When load is 1, you should be able to load a 
  //   16-bit value into the register, when you turn load off, that value should remain in place.
endmodule
